# Fritzing sketch hc sr501 motion sensor fritzing (saved by Fritzing 0.8.4b)
breadboards: 1

parts:
  Part1 = Arduino Uno (Rev3)
  T1 = LM35 Temperature Sensor [package="TO92 [THT]"]
  LED1 = LED - 5mm [color="Red (633nm)" package="5 mm [THT]"]
  R1 = Resistor [tolerance=±5% resistance=220 package=THT]
  J1 = Piezo Speaker

nets:
  N1: Part1.A2, T1.Vout
  N2: Part1.A5/SCL, LED1.anode, J1.pin2
  GND: Part1.GND, T1.GND, R1.Pin_0, J1.pin1
  N3: Part1.5V, T1.+Vs
  N4: LED1.cathode, R1.Pin_1
